# Fritzing sketch Printer Enclosure (saved by Fritzing 0.9.3b)
circuit board: 8.46667cm x 5.64444cm
stripboards: 1

parts:
  M1 = RioRand LM2596
  X1 = USB Connectors [package=usb-a-s]
  X2 = USB Connectors [package=usb-a-s]
  X3 = USB Connectors [package=usb-a-s]
  X4 = USB Connectors [package=usb-a-s]
  4-pin-fan = screw terminal, 4 pins
  PI_CONN = screw terminal, 4 pins
  P_OUT = Screw terminal - 2 pins [package=THT]
  Fuse1 = Fuse with Handler [part_number=Htc-15m]
  R1 = Resistor [tolerance=±5% resistance=100 power=0.25W package="0805 [SMD]"]
  D1 = Zener Diode [part_number=1N4732A breakdown_voltage=3.6V package="Melf DO-213 AB [SMD]"]
  P_OUT2 = Screw terminal - 2 pins [package=THT]
  Q1 = Basic FET N-Channel [part_number=IRF950N package="DPak [SMD]"]
  R2 = Resistor [tolerance=±5% resistance=10k power=0.25W package="0805 [SMD]"]
  P_OUT3 = Screw terminal - 2 pins [package=THT]
  C1 = Capacitor Polarized [package=cpol-radial-100uf-25v]
  P_IN = Screw terminal - 2 pins [package=THT]
  FAN_1 = Screw terminal - 2 pins [package=THT]
  FAN_2 = Screw terminal - 2 pins [package=THT]

nets:
  N1: M1.Pin_1, 4-pin-fan.pin2, P_OUT.pin1, Fuse1.Connector2, P_OUT2.pin1, C1.+, FAN_1.pin1, FAN_2.pin1
  GND: M1.Pin_2, 4-pin-fan.pin1, PI_CONN.pin4, P_OUT.pin2, P_OUT2.pin2, Q1.source, R2.Pin_1, C1.-, P_IN.pin2
  5V: M1.Pin_3, X1.VBUS, X2.VBUS, X3.VBUS, X4.VBUS, P_OUT3.pin1
  GND_2: M1.Pin_4, X1.GND, X2.GND, X3.GND, X4.GND, P_OUT3.pin2
  N2: 4-pin-fan.pin3, PI_CONN.pin2
  N3: 4-pin-fan.pin4, PI_CONN.pin1
  N4: PI_CONN.pin3, R1.Pin_0, D1.cathode
  12V: Fuse1.Connector1, P_IN.pin1
  N5: R1.Pin_1, D1.anode, Q1.Gate, R2.Pin_0
  N6: Q1.drain, FAN_1.pin2, FAN_2.pin2
